// Logisim project Logic01.circ as structural Verilog: 1 circuit, main circuit main
module main (
  input  in_1,
  input  in_2,
  input  in_3,
  input  in_4,
  input  in_5,
  input  A,
  input  in_7,
  input  sel,
  input  B,
  input  in_10,
  input  A_2,
  input  sel_3,
  input  B_2,
  input  sel_1,
  input  sel_2,
  input  A_3,
  input  B_3,
  input  C,
  input  D,
  input  \input ,
  input  sel_4,
  input  in_22,
  input  in_23,
  input  in_24,
  output out_25,
  output out_26,
  output out_27,
  output out_28,
  output A_4,
  output \output ,
  output B_4,
  output output_2,
  output A_5,
  output B_5,
  output A_6,
  output B_6,
  output C_2,
  output D_2
);

  wire and_1_out, and_2_out, and_3_out, and_4_out, nand_2_out, nand_3_out, nand_4_out, nand_5_out,
       nand_6_out, nand_7_out, nand_8_out, nand_11_out, nand_12_out, nand_13_out, nand_14_out, nand_15_out,
       nand_16_out, nand_20_out, nand_21_out, nand_23_out, nand_24_out, nand_25_out, nand_26_out,
       nand_27_out, nand_28_out, nand_29_out, NOT_2_out, not_3_out, not_4_out, not_5_out, not_6_out, NOT_out;

  nand nand_1 (out_25, in_1, in_1);
  nand nand_2 (nand_2_out, in_2, in_3);
  nand nand_3 (nand_3_out, in_4, in_4);
  nand nand_4 (nand_4_out, in_5, in_5);
  nand NOT (NOT_out, in_7, in_7);
  nand NOT_2 (NOT_2_out, in_10, in_10);
  nand nand_5 (nand_5_out, sel_3, sel_3);
  not not_3 (not_3_out, sel_1);
  not not_4 (not_4_out, sel_2);
  not not_5 (not_5_out, in_23);
  not not_6 (not_6_out, in_24);
  nand nand_6 (nand_6_out, sel_3, A_2);
  nand nand_7 (nand_7_out, nand_5_out, B_2);
  and and_1 (and_1_out, A_3, not_4_out, not_3_out);
  and and_2 (and_2_out, B_3, not_4_out, sel_1);
  and and_3 (and_3_out, C, sel_2, not_3_out);
  and and_4 (and_4_out, D, sel_2, sel_1);
  nand nand_8 (nand_8_out, sel_4, sel_4);
  nand nand_9 (out_26, nand_2_out, nand_2_out);
  nand nand_10 (out_27, nand_3_out, nand_4_out);
  nand nand_11 (nand_11_out, in_7, NOT_2_out);
  nand nand_12 (nand_12_out, NOT_out, in_10);
  nand nand_13 (nand_13_out, \input , nand_8_out);
  nand nand_14 (nand_14_out, sel_4, \input );
  and and_5 (A_6, in_22, not_6_out, not_5_out);
  and and_6 (B_6, in_22, not_6_out, in_23);
  and and_7 (C_2, in_22, not_5_out, in_24);
  and and_8 (D_2, in_22, in_23, in_24);
  nand nand_15 (nand_15_out, nand_11_out, nand_11_out);
  nand nand_16 (nand_16_out, nand_12_out, nand_12_out);
  nand nand_17 (\output , nand_6_out, nand_7_out);
  or or_1 (output_2, and_1_out, and_2_out, and_3_out, and_4_out);
  nand nand_18 (A_5, nand_13_out, nand_13_out);
  nand nand_19 (B_5, nand_14_out, nand_14_out);
  nand nand_20 (nand_20_out, nand_15_out, nand_15_out);
  nand nand_21 (nand_21_out, nand_16_out, nand_16_out);
  nand nand_22 (out_28, nand_20_out, nand_21_out);
  nand nand_23 (nand_23_out, sel, sel);
  nand nand_24 (nand_24_out, sel, A);
  nand nand_25 (nand_25_out, nand_23_out, B);
  nand nand_26 (nand_26_out, sel, sel);
  nand nand_27 (nand_27_out, nand_29_out, sel);
  nand nand_28 (nand_28_out, nand_26_out, nand_29_out);
  nand nand_29 (nand_29_out, nand_24_out, nand_25_out);
  nand nand_30 (A_4, nand_27_out, nand_27_out);
  nand nand_31 (B_4, nand_28_out, nand_28_out);

  // Notes on the sheet:
  //   NOT
  //   AND
  //   OR
  //   XOR
  //   2 WAY MUX
  //   4 WAY MUX
  //   2 WAY DMUX
  //   4 WAY DMUX
  //   Nathan Tompkins | Elementary Logic Gates, MUX and DMUX
  //   AND
  //   AND
  //   OR
  //   MUX to DMUX
  //   Just for fun...
  //   input
endmodule
